# Fritzing sketch 12v 12 cells (saved by Fritzing 0.9.3b)
# 18650 Li-ion Battery: CC-BY Dr Kristofer Chan, King's College London/Remote-research.org

parts:
  BAT1 = 18650 Li-ion Battery [package=battery-18650]
  BAT2 = 18650 Li-ion Battery [package=battery-18650]
  BAT3 = 18650 Li-ion Battery [package=battery-18650]
  BAT4 = 18650 Li-ion Battery [package=battery-18650]
  BAT5 = 18650 Li-ion Battery [package=battery-18650]
  BAT6 = 18650 Li-ion Battery [package=battery-18650]
  BAT7 = 18650 Li-ion Battery [package=battery-18650]
  BAT8 = 18650 Li-ion Battery [package=battery-18650]
  BAT9 = 18650 Li-ion Battery [package=battery-18650]
  BAT10 = 18650 Li-ion Battery [package=battery-18650]
  BAT11 = 18650 Li-ion Battery [package=battery-18650]
  BAT12 = 18650 Li-ion Battery [package=battery-18650]
  Mod1 = 3S-BMS
  A3 = WMYCONGCONG buck converter
  J3 = Power Jack [package=power_jack_combo]
  J4 = Power Jack [package=power_jack_combo]
  S2 = Round Pushbutton
  LED2 = smd LED [color="Red (633nm)" package="1206 [SMD]"]
  R2 = Resistor [tolerance=±5% resistance=220 package=THT]
  D2 = Rectifier Diode [part_number=1N4001 package="300 mil [THT]"]
  D3 = Rectifier Diode [part_number=1N4001 package="300 mil [THT]"]

nets:
  N1: BAT1.-, BAT4.-, Mod1.0V
  N2: BAT1.+, BAT2.+, BAT3.+, BAT5.-, BAT6.-, BAT7.-, Mod1.4.2V
  N3: BAT4.+, BAT8.-
  N4: BAT5.+, BAT8.+, BAT9.-, BAT12.-, Mod1.8.4V
  N5: BAT6.+, BAT10.-
  N6: BAT7.+, BAT11.-
  N7: BAT9.+, BAT12.+, Mod1.12.6V
  N8: A3.Pin_1, J4.GND
  N9: A3.Pin_2, S2.leg1
  N10: A3.Pin_4, D3.cathode
  N11: J3.GND, J3.GNDBREAK, LED2.cathode, R2.Pin_1, D2.anode
  N12: J4.GNDBREAK, D3.anode
  N13: S2.leg0, D2.cathode

custom parts:
  18650 Li-ion Battery: 18650 li-ion Battery Standard 18650 battery with interactive connectors Creative Common Attribution 4.0 International (CC-BY 4.0) license. Any use of this part requires attribution of Dr Kristofer Chan, Department of Geography, King's College London. Contact kristofer.chan [at] kcl.ac.uk OR kris [at] remote-research.org for further information.
  3S-BMS: 3S-BMS LIPO battery charger / protection unit. Note pcb does not match the board as it will likely connect with wires, so pcb is 6 pads suitable for .1in header pins.
  WMYCONGCONG buck converter: These amazing little DC-DC converters feature a wide input voltage of 4.5-24V and the output voltage can be set to one of six fixed voltages, or fully variable, just by bridging the relevant solder pads on the back of the PCB..
  Round Pushbutton: A generic pushbutton.
